// Logisim project ex2.circ as structural Verilog: 1 circuit, main circuit compute_BrUn
module compute_BrUn (
  input  [31:0] INSTRUCTION,
  output BrUn
);

  wire comparator_1_eq, comparator_2_eq;

  Comparator #(.mode("unsigned"), .width(3)) comparator_1 (
    .a(INSTRUCTION[14:12]), .b(3'b110), .eq(comparator_1_eq));  // open: gt, lt
  Comparator #(.mode("unsigned"), .width(3)) comparator_2 (
    .a(INSTRUCTION[14:12]), .b(3'b111), .eq(comparator_2_eq));  // open: gt, lt
  or or_1 (BrUn, comparator_1_eq, comparator_2_eq);
endmodule
